# Fritzing sketch schema (saved by Fritzing 0.7.11b)
breadboards: 1

parts:
  Arduino1 = Arduino
  IR1 = TSOP312.., 314.. [package=THT]

nets:
  N1: Arduino1.D2, IR1.GND
  N2: Arduino1.+5V, IR1.Data
  N3: Arduino1.GND, IR1.Vs
